# Fritzing sketch flex_sensors_dc_motors (saved by Fritzing 0.9.2b)
circuit board: 8.46667cm x 5.64444cm
breadboards: 2

parts:
  R1 = Resistor [tolerance=±5% resistance=22k package=THT]
  R2 = Basic Flex Resistor
  Part1 = Arduino Uno (Rev3)
  R3 = Basic Flex Resistor
  R4 = Resistor [tolerance=±5% resistance=22k package=THT]
  R5 = Basic Flex Resistor
  R6 = Resistor [tolerance=±5% resistance=22k package=THT]
  R8 = Resistor [tolerance=±5% resistance=22k package=THT]
  R10 = Resistor [tolerance=±5% resistance=22k package=THT]
  U1 = Voltage Regulator - 5V [package="TO220 [THT]"]
  J1 = Basic Force Sensing Resistor (FSR) [package=THT]
  J2 = Basic Force Sensing Resistor (FSR) [package=THT]
  D1 = Rectifier Diode [part_number=1N4001 package="300 mil [THT]"]
  R11 = Resistor [tolerance=±5% resistance=10k package=THT]
  M1 = DC Motor
  R12 = Resistor [tolerance=±5% resistance=10k package=THT]
  D2 = Rectifier Diode [part_number=1N4001 package="300 mil [THT]"]
  M2 = DC Motor
  R13 = Resistor [tolerance=±5% resistance=10k package=THT]
  D3 = Rectifier Diode [part_number=1N4001 package="300 mil [THT]"]
  M3 = DC Motor
  R14 = Resistor [tolerance=±5% resistance=10k package=THT]
  D4 = Rectifier Diode [part_number=1N4001 package="300 mil [THT]"]
  M4 = DC Motor
  R15 = Resistor [tolerance=±5% resistance=10k package=THT]
  D5 = Rectifier Diode [part_number=1N4001 package="300 mil [THT]"]
  M5 = DC Motor
  U2 = Voltage Regulator - 5V [package="TO220 [THT]"]
  U3 = Voltage Regulator - 5V [package="TO220 [THT]"]
  U4 = Voltage Regulator - 5V [package="TO220 [THT]"]
  U5 = Voltage Regulator - 5V [package="TO220 [THT]"]
  VCC1 = Battery

nets:
  N1: R1.Pin_0, R2.Pin_2, Part1.A4/SDA
  N2: R1.Pin_1, Part1.GND, R4.Pin_1, R6.Pin_1, R8.Pin_1, R10.Pin_1, U1.output_voltage, R11.Pin_1, R12.Pin_1, R13.Pin_1, R14.Pin_1, R15.Pin_1, U2.output_voltage, U3.output_voltage, U4.output_voltage, U5.output_voltage, VCC1.-
  N3: R2.pin_1, Part1.5V, R3.pin_1, R5.pin_1, J1.pin_0, J2.pin_0
  N4: Part1.A0, R8.Pin_0, J1.pin_1
  N5: Part1.A1, R10.Pin_0, J2.pin_1
  N6: Part1.A2, R5.Pin_2, R6.Pin_0
  N7: Part1.A3, R3.Pin_2, R4.Pin_0
  N8: Part1.D8, R15.Pin_0, U5.input_voltage
  N9: Part1.D9_PWM, R14.Pin_0, U4.input_voltage
  N10: Part1.D10_PWM/SS, R13.Pin_0, U3.input_voltage
  N11: Part1.D11_PWM/MOSI, R12.Pin_0, U2.input_voltage
  N12: Part1.D12/MISO, U1.input_voltage, R11.Pin_0
  N13: U1.GND, D1.anode, M1.pin_1
  N14: D1.cathode, M1.pin_2, D2.cathode, M2.pin_2, D3.cathode, M3.pin_2, D4.cathode, M4.pin_2, D5.cathode, M5.pin_2, VCC1.+
  N15: D2.anode, M2.pin_1, U2.GND
  N16: D3.anode, M3.pin_1, U3.GND
  N17: D4.anode, M4.pin_1, U4.GND
  N18: D5.anode, M5.pin_1, U5.GND
