# Fritzing sketch arduinos_RF_transmiter_receiver (saved by Fritzing 0.9.2b)
breadboards: 2

parts:
  Part1 = Arduino Micro (Rev3)  # not connected
  S1 = Pushbutton [package="[THT]"]
  U1 = RF-LINK_TX [package=rf-link_tx]
  U2 = RF-LINK_RX [package=rf-link_rx]
  R1 = Resistor [tolerance=±5% resistance=10k package="2512 [SMD]"]
  LED1 = smd LED [color="Red (633nm)" package="0805 [SMD]"]
  LED3 = smd LED [color="Red (633nm)" package="0805 [SMD]"]
  Part2 = Arduino Uno (Rev3) - ICSP
  LED4 = smd LED [color="Red (633nm)" package="0805 [SMD]"]
  U3 = RF-LINK_RX [package=rf-link_rx]
  U4 = RF-LINK_TX [package=rf-link_tx]
  S2 = Pushbutton [package="[THT]"]
  R2 = Resistor [tolerance=±5% resistance=10k package="2512 [SMD]"]

nets:
  N1: S1.Pin_1, S1.Pin_2, U1.ANT
  N2: S1.Pin_3, S1.Pin_4, R1.Pin_0
  N3: U1.DATA, U2.+5V, R1.Pin_1
  N4: U2.DATA, U2.ANT, LED1.cathode, LED3.cathode
  N5: Part2.D8, LED4.anode
  N6: Part2.GND, LED4.cathode, U3.DATA, U3.ANT, S2.Pin_1, S2.Pin_2
  N7: Part2.D3_PWM, S2.Pin_3, S2.Pin_4, R2.Pin_1
  N8: Part2.D4, U4.+5V
  5V: Part2.5V, U3.+5V, U4.DATA, R2.Pin_0
